// Logisim project 152120211104_1.10.circ as structural Verilog: 1 circuit, main circuit PART 1.1 NAND
module PART_1_1_NAND (
  input  S1_1,
  input  S1_2,
  output out_3
);

  nand nand_1 (out_3, S1_1, S1_2);

  // Notes on the sheet:
  //   1
  //   2
endmodule
