// Logisim project 152120211104_1.11.circ as structural Verilog: 1 circuit, main circuit PART 1.1 NOR
module PART_1_1_NOR (
  input  S1_1,
  input  S1_2,
  output out_3
);

  nor nor_1 (out_3, S1_1, S1_2);

  // Notes on the sheet:
  //   1
  //   2
endmodule
