// Logisim project 152120211104_1.12.circ as structural Verilog: 1 circuit, main circuit PART 1.1 AND
module PART_1_1_AND (
  input  S1_1,
  input  S1_2,
  output out_3
);

  and and_1 (out_3, S1_1, S1_2);

  // Notes on the sheet:
  //   1
  //   2
endmodule
