// Logisim project 152120211104_1.13.circ as structural Verilog: 1 circuit, main circuit PART 1.1 OR
module PART_1_1_OR (
  input  S1_1,
  input  S1_2,
  output out_3
);

  or or_1 (out_3, S1_1, S1_2);

  // Notes on the sheet:
  //   1
  //   2
endmodule
