// Logisim project 152120211104_1.14.circ as structural Verilog: 1 circuit, main circuit PART 1.1 XOR
module PART_1_1_XOR (
  input  S1_1,
  input  S1_2,
  output out_3
);

  xor xor_1 (out_3, S1_1, S1_2);
endmodule
