// Logisim project 152120211104_1.50.circ as structural Verilog: 1 circuit, main circuit PART 1.45 Inverter
module PART_1_45_Inverter (
  input  S1_1,
  output out_2
);

  not not_1 (out_2, S1_1);
endmodule
