// Logisim project 152120211104_2.10.circ as structural Verilog: 1 circuit, main circuit PART 2 Figure 4
module PART_2_Figure_4 (
  input  A,
  input  B,
  output E
);

  wire nand_1_out, nor_1_out;

  nor nor_1 (nor_1_out, A, B);
  nand nand_1 (nand_1_out, A, B);
  xor xor_1 (E, nor_1_out, nand_1_out);

  // Notes on the sheet:
  //   C
  //   D
endmodule
