// Logisim project 152120211104_2.11.circ as structural Verilog: 1 circuit, main circuit PART 2 Figure 5
module PART_2_Figure_5 (
  input  A,
  input  B,
  output D
);

  wire nand_1_out;

  nand nand_1 (nand_1_out, B, B);
  nand nand_2 (D, A, nand_1_out);

  // Notes on the sheet:
  //   C
endmodule
