// Logisim project 152120211104_3.10.circ as structural Verilog: 1 circuit, main circuit PART 3 Figure 1
module PART_3_Figure_1 (
  input  X1,
  input  X2,
  output Y
);

  wire nand_1_out, nand_2_out;

  nand nand_1 (nand_1_out, X1, X1);
  nand nand_2 (nand_2_out, X2, X2);
  nand nand_3 (Y, nand_1_out, nand_2_out);
endmodule
