// Logisim project 152120211104_3.11.circ as structural Verilog: 1 circuit, main circuit PART 3 Figure 2
module PART_3_Figure_2 (
  input  X1,
  input  X2,
  output Y
);

  wire nand_1_out;

  nand nand_1 (nand_1_out, X1, X2);
  nand nand_2 (Y, nand_1_out, nand_1_out);
endmodule
