// Logisim project 152120211104_3.12.circ as structural Verilog: 1 circuit, main circuit PART 3 Figure 3
module PART_3_Figure_3 (
  input  X1,
  input  X2,
  output Y1,
  output Y2
);

  wire nor_1_out;

  nor nor_1 (nor_1_out, X1, X2);
  and and_1 (Y2, X1, X2);
  nor nor_2 (Y1, nor_1_out, Y2);
endmodule
