// Logisim project 152120211104_3.14.circ as structural Verilog: 1 circuit, main circuit PART 3 Figure 5
module PART_3_Figure_5 (
  input  X1,
  input  X2,
  input  X1_2,
  output Y
);

  wire xor_1_out;

  xor xor_1 (xor_1_out, X1, X2);
  xor xor_2 (Y, xor_1_out, X1_2);
endmodule
