// Logisim project 152120211104_3.20.circ as structural Verilog: 1 circuit, main circuit main
module main (
  input  in_1,
  input  in_2,
  input  in_3,
  input  in_4,
  output out_5
);

  nor nor_1 (out_5, in_1, in_2, in_3, in_4);
endmodule
