// Logisim project 152120211104.circ as structural Verilog: 2 circuits, main circuit main
module main (
);

  wire _7493_q1, _7493_q2, _7493_q3, _7493_q4, clock_1_out, clock_2_out, ic_7493_1_p2, ic_7493_1_p6,
       ic_7493_1_p7, ic_7493_1_p8, n7_segment_display_driver_1_a_2, n7_segment_display_driver_1_b_2,
       n7_segment_display_driver_1_c_2, n7_segment_display_driver_1_d_2, n7_segment_display_driver_1_e,
       n7_segment_display_driver_1_f, n7_segment_display_driver_1_g, n7_segment_display_driver_2_a_2,
       n7_segment_display_driver_2_b_2, n7_segment_display_driver_2_c_2, n7_segment_display_driver_2_d_2,
       n7_segment_display_driver_2_e, n7_segment_display_driver_2_f, n7_segment_display_driver_2_g;

  Clock clock_1 (.out(clock_1_out));
  Clock clock_2 (.out(clock_2_out));
  _7493 _7493 (
    .CLK0(clock_1_out), .CLK1(_7493_q1), .CLR1(_7493_q2), .CLR2(_7493_q4), .Q1(_7493_q1), .Q2(_7493_q2),
    .Q3(_7493_q3), .Q4(_7493_q4));
  // IC_7493 ic_7493_1: pin names not known; wires that end beside it: clock_2_out, ic_7493_1_p2, 1'b0, 1'b0, ic_7493_1_p2, ic_7493_1_p6, ic_7493_1_p7, ic_7493_1_p8
  _7_segment_display_driver u_7_segment_display_driver_1 (
    .D(ic_7493_1_p8), .C(ic_7493_1_p7), .B(ic_7493_1_p6), .A(ic_7493_1_p2),
    .a_2(n7_segment_display_driver_1_a_2), .b_2(n7_segment_display_driver_1_b_2),
    .c_2(n7_segment_display_driver_1_c_2), .d_2(n7_segment_display_driver_1_d_2),
    .e(n7_segment_display_driver_1_e), .f(n7_segment_display_driver_1_f), .g(n7_segment_display_driver_1_g));
  _7_segment_display_driver u_7_segment_display_driver_2 (
    .D(_7493_q4), .C(_7493_q3), .B(_7493_q2), .A(_7493_q1), .a_2(n7_segment_display_driver_2_a_2),
    .b_2(n7_segment_display_driver_2_b_2), .c_2(n7_segment_display_driver_2_c_2),
    .d_2(n7_segment_display_driver_2_d_2), .e(n7_segment_display_driver_2_e),
    .f(n7_segment_display_driver_2_f), .g(n7_segment_display_driver_2_g));
  _7_Segment_Display u_7_segment_display_1 (
    .g(n7_segment_display_driver_1_g), .f(n7_segment_display_driver_1_f),
    .a(n7_segment_display_driver_1_a_2), .b(n7_segment_display_driver_1_b_2),
    .e(n7_segment_display_driver_1_e), .d(n7_segment_display_driver_1_d_2),
    .c(n7_segment_display_driver_1_c_2));  // open: dp
  _7_Segment_Display u_7_segment_display_2 (
    .g(n7_segment_display_driver_2_g), .f(n7_segment_display_driver_2_f),
    .a(n7_segment_display_driver_2_a_2), .b(n7_segment_display_driver_2_b_2),
    .e(n7_segment_display_driver_2_e), .d(n7_segment_display_driver_2_d_2),
    .c(n7_segment_display_driver_2_c_2));  // open: dp

  // Notes on the sheet:
  //   Önemli Bit
  //   Onemli Bit
  //   Figure 4
  //   Onemli Bit=D
  //   Onemli Bit
  //   Figure 5
endmodule

module _7493 (
  input  CLK0,
  input  CLK1,
  input  CLR1,
  input  CLR2,
  output Q1,
  output Q2,
  output Q3,
  output Q4
);

  wire and_1_out, d_flip_flop_1_p1, d_flip_flop_2_p1, d_flip_flop_3_p1, d_flip_flop_4_p1, not_1_out,
       not_2_out, not_3_out, not_4_out;

  and and_1 (and_1_out, CLR1, CLR2);
  not not_1 (not_1_out, CLK0);
  not not_2 (not_2_out, CLK1);
  not not_3 (not_3_out, Q2);
  not not_4 (not_4_out, Q3);
  // D_Flip_Flop d_flip_flop_1: pin names not known; wires that end beside it: d_flip_flop_1_p1, not_1_out, and_1_out, Q1, d_flip_flop_1_p1
  // D_Flip_Flop d_flip_flop_2: pin names not known; wires that end beside it: d_flip_flop_2_p1, not_2_out, and_1_out, Q2, d_flip_flop_2_p1
  // D_Flip_Flop d_flip_flop_3: pin names not known; wires that end beside it: d_flip_flop_3_p1, not_3_out, and_1_out, Q3, d_flip_flop_3_p1
  // D_Flip_Flop d_flip_flop_4: pin names not known; wires that end beside it: d_flip_flop_4_p1, not_4_out, and_1_out, Q4, d_flip_flop_4_p1
endmodule
