// Logisim project 152120211104_01.circ as structural Verilog: 1 circuit, main circuit main
module main (
  input  A,
  input  [2:0] B_C_D,
  input  Enable
);

  wire n74151_1_p5, not_1_out;

  LED P (.in(n74151_1_p5));
  not not_1 (not_1_out, A);
  // _74151 74151_1: pin names not known; wires that end beside it: not_1_out, A, A, not_1_out, n74151_1_p5, Enable, 1'b0, 1'b1, A, not_1_out, not_1_out, A, B_C_D[2], B_C_D[1], B_C_D[0]
endmodule
