// Logisim project 152120211104_02.circ as structural Verilog: 1 circuit, main circuit main
module main (
  input  C,
  input  Enable,
  input  D,
  input  A_Select,
  input  B_Select
);

  wire and_1_out, and_2_out, multiplexer_1_out, not_1_out, not_2_out, or_1_out, xor_1_out;

  not not_1 (not_1_out, C);
  not not_2 (not_2_out, D);
  and and_1 (and_1_out, C, D);
  and and_2 (and_2_out, not_1_out, not_2_out);
  xor xor_1 (xor_1_out, C, D);
  or or_1 (or_1_out, and_1_out, and_2_out);
  Multiplexer #(.select(2)) multiplexer_1 (
    .in0(or_1_out), .in1(xor_1_out), .in2(xor_1_out), .in3(or_1_out), .out(multiplexer_1_out),
    .sel({B_Select, A_Select}), .en(Enable));
  LED P (.in(multiplexer_1_out));
endmodule
