// Logisim project 152120211104_03.circ as structural Verilog: 1 circuit, main circuit 74154
module _74154 (
  input  iE0,
  input  iE1,
  input  B0,
  input  B1,
  input  A0,
  input  A1,
  output Z0,
  output Z1
);

  wire decoder_1_out0, decoder_1_out1, decoder_1_out2, decoder_1_out3, decoder_1_out4, decoder_1_out5,
       decoder_1_out6, decoder_1_out7, decoder_1_out8, decoder_1_out9, decoder_1_out10, decoder_1_out11,
       decoder_1_out12, decoder_1_out13, decoder_1_out14, decoder_1_out15, nor_1_out, not_1_out, not_2_out,
       not_3_out, not_4_out, not_5_out, not_6_out, not_7_out, not_8_out, not_9_out, not_10_out, not_11_out,
       not_12_out, not_13_out, not_14_out, not_15_out, not_16_out;
  wire [3:0] buffer_1_out;

  not not_1 (not_1_out, decoder_1_out0);
  not not_2 (not_2_out, decoder_1_out1);
  not not_3 (not_3_out, decoder_1_out2);
  not not_4 (not_4_out, decoder_1_out3);
  not not_5 (not_5_out, decoder_1_out4);
  not not_6 (not_6_out, decoder_1_out5);
  not not_7 (not_7_out, decoder_1_out6);
  not not_8 (not_8_out, decoder_1_out7);
  not not_9 (not_9_out, decoder_1_out8);
  not not_10 (not_10_out, decoder_1_out9);
  not not_11 (not_11_out, decoder_1_out10);
  not not_12 (not_12_out, decoder_1_out11);
  not not_13 (not_13_out, decoder_1_out12);
  not not_14 (not_14_out, decoder_1_out13);
  not not_15 (not_15_out, decoder_1_out14);
  not not_16 (not_16_out, decoder_1_out15);
  Decoder #(.select(4), .disabled(0)) decoder_1 (
    .out0(decoder_1_out0), .out1(decoder_1_out1), .out2(decoder_1_out2), .out3(decoder_1_out3),
    .out4(decoder_1_out4), .out5(decoder_1_out5), .out6(decoder_1_out6), .out7(decoder_1_out7),
    .out8(decoder_1_out8), .out9(decoder_1_out9), .out10(decoder_1_out10), .out11(decoder_1_out11),
    .out12(decoder_1_out12), .out13(decoder_1_out13), .out14(decoder_1_out14), .out15(decoder_1_out15),
    .sel(buffer_1_out), .en(nor_1_out));
  nor nor_1 (nor_1_out, iE0, iE1);
  assign buffer_1_out = {A1, A0, B1, B0};  // Buffer buffer_1, 4 bits wide
  nand nand_1 (Z0, not_2_out, not_4_out, not_5_out, not_7_out, not_10_out, not_12_out, not_13_out, not_15_out);
  nand nand_2 (Z1, not_1_out, not_3_out, not_6_out, not_8_out, not_9_out, not_11_out, not_14_out, not_16_out);

  // Notes on the sheet:
  //   74154  
endmodule
