// Logisim project 152120211104_04.circ as structural Verilog: 2 circuits, main circuit main
module main (
  input  B0,
  input  A1,
  input  B1,
  input  A0,
  output Z0,
  output Z1
);

  wire n3x8_1_y0, n3x8_1_y1, n3x8_1_y2, n3x8_1_y3, n3x8_1_y4, n3x8_1_y5, n3x8_1_y6, n3x8_1_y7, n3x8_2_y0,
       n3x8_2_y1, n3x8_2_y2, n3x8_2_y3, n3x8_2_y4, n3x8_2_y5, n3x8_2_y6, n3x8_2_y7, not_1_out, not_2_out,
       not_3_out, not_4_out, not_5_out, not_6_out, not_7_out, not_8_out, not_9_out, not_10_out, not_11_out,
       not_12_out, not_13_out, not_14_out, not_15_out, not_16_out, not_17_out;

  not not_1 (not_1_out, A1);
  _3x8 u_3x8_1 (
    .A1(not_1_out), .A0(A0), .B1(B1), .B0(B0), .Y0(n3x8_1_y0), .Y1(n3x8_1_y1), .Y2(n3x8_1_y2),
    .Y3(n3x8_1_y3), .Y4(n3x8_1_y4), .Y5(n3x8_1_y5), .Y6(n3x8_1_y6), .Y7(n3x8_1_y7));
  _3x8 u_3x8_2 (
    .A1(A1), .A0(A0), .B1(B1), .B0(B0), .Y0(n3x8_2_y0), .Y1(n3x8_2_y1), .Y2(n3x8_2_y2), .Y3(n3x8_2_y3),
    .Y4(n3x8_2_y4), .Y5(n3x8_2_y5), .Y6(n3x8_2_y6), .Y7(n3x8_2_y7));
  not not_2 (not_2_out, n3x8_1_y0);
  not not_3 (not_3_out, n3x8_1_y1);
  not not_4 (not_4_out, n3x8_1_y2);
  not not_5 (not_5_out, n3x8_1_y3);
  not not_6 (not_6_out, n3x8_1_y4);
  not not_7 (not_7_out, n3x8_1_y5);
  not not_8 (not_8_out, n3x8_1_y6);
  not not_9 (not_9_out, n3x8_1_y7);
  not not_10 (not_10_out, n3x8_2_y0);
  not not_11 (not_11_out, n3x8_2_y1);
  not not_12 (not_12_out, n3x8_2_y2);
  not not_13 (not_13_out, n3x8_2_y3);
  not not_14 (not_14_out, n3x8_2_y4);
  not not_15 (not_15_out, n3x8_2_y5);
  not not_16 (not_16_out, n3x8_2_y6);
  not not_17 (not_17_out, n3x8_2_y7);
  nand nand_1 (Z0, not_2_out, not_4_out, not_7_out, not_9_out, not_10_out, not_12_out, not_15_out, not_17_out);
  nand nand_2 (Z1, not_3_out, not_5_out, not_6_out, not_8_out, not_11_out, not_13_out, not_14_out, not_16_out);
endmodule

module _3x8 (
  input  A1,
  input  A0,
  input  B1,
  input  B0,
  output Y0,
  output Y1,
  output Y2,
  output Y3,
  output Y4,
  output Y5,
  output Y6,
  output Y7
);

  wire not_1_out, not_2_out, not_3_out;

  not not_1 (not_1_out, A0);
  not not_2 (not_2_out, B1);
  not not_3 (not_3_out, B0);
  and and_1 (Y0, A1, not_1_out, not_2_out, not_3_out);
  and and_2 (Y1, A1, not_1_out, not_2_out, B0);
  and and_3 (Y2, A1, not_1_out, B1, not_3_out);
  and and_4 (Y3, A1, not_1_out, B1, B0);
  and and_5 (Y4, A1, A0, not_2_out, not_3_out);
  and and_6 (Y5, A1, A0, not_2_out, B0);
  and and_7 (Y6, A1, A0, B1, not_3_out);
  and and_8 (Y7, A1, A0, B1, B0);
endmodule
