// Logisim project 152120211104_P1.circ as structural Verilog: 1 circuit, main circuit main
module main (
  input  Cin,
  input  [3:0] A0_A4,
  input  [3:0] B0_B4,
  output [3:0] S0_S4,
  output Cout
);

  wire adder_1_cout, adder_2_cout, adder_3_cout, xor_1_out, xor_2_out, xor_3_out, xor_4_out;

  xor xor_1 (xor_1_out, B0_B4[0], Cin);
  xor xor_2 (xor_2_out, B0_B4[1], Cin);
  xor xor_3 (xor_3_out, B0_B4[2], Cin);
  xor xor_4 (xor_4_out, B0_B4[3], Cin);
  Adder #(.width(1)) adder_1 (.a(A0_A4[0]), .b(xor_1_out), .out(S0_S4[0]), .cin(Cin), .cout(adder_1_cout));
  Adder #(.width(1)) adder_2 (.a(A0_A4[1]), .b(xor_2_out), .out(S0_S4[1]), .cin(adder_1_cout), .cout(adder_2_cout));
  Adder #(.width(1)) adder_3 (.a(A0_A4[2]), .b(xor_3_out), .out(S0_S4[2]), .cin(adder_2_cout), .cout(adder_3_cout));
  Adder #(.width(1)) adder_4 (.a(A0_A4[3]), .b(xor_4_out), .out(S0_S4[3]), .cin(adder_3_cout), .cout(Cout));
endmodule
