// Logisim project 152120211104_Q1.circ as structural Verilog: 1 circuit, main circuit main
module main (
  input  X,
  input  Y,
  input  X_2,
  input  Y_2,
  input  Z,
  output S,
  output C,
  output S_2,
  output C_2
);

  wire nand_1_out, nand_2_out, nand_4_out, nand_5_out, xor_1_out;

  xor xor_1 (xor_1_out, X_2, Y_2);
  nand nand_1 (nand_1_out, X, Y);
  nand nand_2 (nand_2_out, X, Y);
  xor xor_2 (S_2, xor_1_out, Z);
  xor xor_3 (S, X, Y);
  nand nand_3 (C, nand_1_out, nand_2_out);
  nand nand_4 (nand_4_out, X_2, Y_2);
  nand nand_5 (nand_5_out, S_2, Z);
  nand nand_6 (C_2, nand_4_out, nand_5_out);

  // Notes on the sheet:
  //   Half Adder
  //   Full Adder
endmodule
