// Logisim project 152120211104_Q2.circ as structural Verilog: 1 circuit, main circuit main
module main (
  input  C,
  output Q,
  output Q_prime
);

  wire D_out, nand_1_out, nand_2_out, not_1_out;

  Clock D (.out(D_out));
  not not_1 (not_1_out, D_out);
  nand nand_1 (nand_1_out, D_out, C);
  nand nand_2 (nand_2_out, C, not_1_out);
  nand nand_3 (Q, nand_1_out, Q_prime);
  nand nand_4 (Q_prime, Q, nand_2_out);
endmodule
