// Logisim project 152120211104_Q3.circ as structural Verilog: 1 circuit, main circuit main
module main (
  input  J,
  input  K,
  input  Preset,
  input  Clear,
  output Q,
  output Q_prime
);

  wire clock_1_out, not_1_out, not_2_out, not_3_out;

  not not_1 (not_1_out, Preset);
  not not_2 (not_2_out, Clear);
  Clock clock_1 (.out(clock_1_out));
  not not_3 (not_3_out, clock_1_out);
  // _7476 7476_1: pin names not known; wires that end beside it: not_3_out, not_1_out, not_2_out, J, K, Q, Q_prime
endmodule
