// Logisim project 152120211104_Q4.circ as structural Verilog: 1 circuit, main circuit main
module main (
  input  Preset,
  input  Clear,
  input  D,
  output Q,
  output Q_prime
);

  wire clock_1_out, not_1_out, not_2_out;

  not not_1 (not_1_out, Preset);
  not not_2 (not_2_out, Clear);
  Clock clock_1 (.out(clock_1_out));
  // _7474 7474_1: pin names not known; wires that end beside it: not_2_out, D, clock_1_out, not_1_out, Q, Q_prime
endmodule
