// Logisim project 152120211104_Q1.circ as structural Verilog: 1 circuit, main circuit main
module main (
  input  X,
  output A_Next_State,
  output B_Next_State,
  output Z
);

  wire and_1_out, and_2_out, and_3_out, and_4_out, and_5_out, and_6_out, clock_1_out, not_1_out, not_2_out,
       not_3_out, not_4_out, not_5_out, or_1_out, or_2_out;

  Clock clock_1 (.out(clock_1_out));
  not not_1 (not_1_out, X);
  not not_2 (not_2_out, X);
  not not_3 (not_3_out, A_Next_State);
  not not_4 (not_4_out, A_Next_State);
  not not_5 (not_5_out, B_Next_State);
  and and_1 (and_1_out, not_1_out, A_Next_State);
  and and_2 (and_2_out, X, B_Next_State);
  and and_3 (and_3_out, not_2_out, B_Next_State);
  and and_4 (and_4_out, X, not_3_out);
  and and_5 (and_5_out, not_4_out, not_5_out);
  and and_6 (and_6_out, A_Next_State, B_Next_State);
  or or_1 (or_1_out, and_1_out, and_2_out);
  or or_2 (or_2_out, and_3_out, and_4_out);
  or or_3 (Z, and_5_out, and_6_out);
  D_Flip_Flop d_ff_1 (.clk(clock_1_out), .D(or_1_out), .Q(A_Next_State));  // open: Qn, preset, en, reset
  D_Flip_Flop d_ff_2 (.clk(clock_1_out), .D(or_2_out), .Q(B_Next_State));  // open: Qn, preset, en, reset
endmodule
