// Logisim project 152120211104_Q5.circ as structural Verilog: 3 circuits, main circuit main
module main (
  output out_1,
  output out_2,
  output out_3,
  output out_4
);

  wire clock_1_out;

  Clock clock_1 (.out(clock_1_out));
  _7493 u_7493_1 (
    .Clock_0(clock_1_out), .Clock_1(out_1), .Clear_0(out_3), .Clear_1(out_4), .Q1(out_1), .Q2(out_2),
    .Q3(out_3), .Q4(out_4));
endmodule

module D_Flip_Flop (
  input  Clock,
  input  D,
  input  Set,
  input  Clear,
  output Q,
  output R
);

  D_Flip_Flop_part d_ff_1 (.clk(Clock), .D(D), .Q(Q), .Qn(R), .preset(Set), .reset(Clear));  // open: en
endmodule

module _7493 (
  input  Clock_0,
  input  Clock_1,
  input  Clear_0,
  input  Clear_1,
  output Q1,
  output Q2,
  output Q3,
  output Q4
);

  wire and_1_out, d_flip_flop_1_r, d_flip_flop_2_r, d_flip_flop_3_r, d_flip_flop_4_r, not_1_out, not_2_out,
       not_3_out, not_4_out;

  not not_1 (not_1_out, Clock_0);
  not not_2 (not_2_out, Clock_1);
  not not_3 (not_3_out, Q2);
  not not_4 (not_4_out, Q3);
  and and_1 (and_1_out, Clear_0, Clear_1);
  D_Flip_Flop d_flip_flop_1 (
    .Clock(not_1_out), .D(d_flip_flop_1_r), .Clear(and_1_out), .Q(Q1), .R(d_flip_flop_1_r));  // open: Set
  D_Flip_Flop d_flip_flop_2 (
    .Clock(not_2_out), .D(d_flip_flop_2_r), .Clear(and_1_out), .Q(Q2), .R(d_flip_flop_2_r));  // open: Set
  D_Flip_Flop d_flip_flop_3 (
    .Clock(not_3_out), .D(d_flip_flop_3_r), .Clear(and_1_out), .Q(Q3), .R(d_flip_flop_3_r));  // open: Set
  D_Flip_Flop d_flip_flop_4 (
    .Clock(not_4_out), .D(d_flip_flop_4_r), .Clear(and_1_out), .Q(Q4), .R(d_flip_flop_4_r));  // open: Set
endmodule
